// Logisim project cpu.circ as structural Verilog: 7 circuits, main circuit main
module main (
  input  in_1
);

  wire clock_1_out, comparator_1_eq, memorycontroller_1_write_2, not_1_out, not_2_out, tty_1_p5, tty_1_p6,
       tty_1_p9;
  wire [1:0] controlled_buffer_1_out, cpu_1_write;
  wire [6:0] tty_1_p4, tty_1_p7;
  wire [31:0] cpu_1_aout, cpu_1_dout, memorycontroller_1_aout, memorycontroller_1_dout, pull_resistor_1_node,
       ram_1_dout, tty_1_p3;

  Clock clock_1 (.out(clock_1_out));
  Pull_Resistor pull_resistor_1 (.node(pull_resistor_1_node));
  CPU cpu_1 (
    .Clock(clock_1_out), .DIn(tty_1_p3), .Reset(in_1), .Aout(cpu_1_aout), .Dout(cpu_1_dout),
    .Write(cpu_1_write));
  not not_1 (not_1_out, comparator_1_eq);
  Comparator #(.width(32)) comparator_1 (.a(pull_resistor_1_node), .b(tty_1_p3), .eq(comparator_1_eq));  // open: gt, lt
  // TTY tty_1: pin names not known; wires that end beside it: cpu_1_aout, not_1_out, tty_1_p3, tty_1_p4, tty_1_p5, tty_1_p6, tty_1_p7, tty_1_p3, tty_1_p9
  MemoryController memorycontroller_1 (
    .Ain(cpu_1_aout), .Dcur(tty_1_p3), .Din(cpu_1_dout), .Write(cpu_1_write), .Aout(memorycontroller_1_aout),
    .Dout(memorycontroller_1_dout), .write_2(memorycontroller_1_write_2));
  TTY_part #(.asciiwidth(8), .trigger("falling")) tty_2 (.data(tty_1_p4), .clk(clock_1_out), .we(tty_1_p5), .clr(in_1));
  Keyboard #(.asciiwidth(8), .trigger("falling")) keyboard_1 (
    .clk(clock_1_out), .re(tty_1_p6), .clr(in_1), .data(tty_1_p7));  // open: avail
  RAM #(.addrWidth(24), .dataWidth(32), .trigger("falling")) ram_1 (
    .addr(memorycontroller_1_aout[25:2]), .we(memorycontroller_1_write_2), .clk(clock_1_out),
    .din(memorycontroller_1_dout), .dout(ram_1_dout));
  assign controlled_buffer_1_out = memorycontroller_1_write_2 ? memorycontroller_1_aout[1:0] : 2'bz;  // Controlled_Buffer controlled_buffer_1
  Pull_Resistor pull_resistor_2 (.node(controlled_buffer_1_out));
  not not_2 (not_2_out, tty_1_p9);
  Pull_Resistor pull_resistor_3 (.node(tty_1_p9));
  // Probe on tty_1_p3
  MemoryDataController memorydatacontroller_1 (
    .Din(ram_1_dout), .Enable(not_2_out), .LowAddr(controlled_buffer_1_out), .Din_2(tty_1_p3));
endmodule

module CPU (
  input  Clock,
  input  [31:0] DIn,
  input  Reset,
  output [31:0] Aout,
  output [31:0] Dout,
  output [1:0] Write
);

  PC pc_1 (.Clock(Clock), .Reset(Reset), .A_Out(Aout));  // open: AddrOff, A_IN, AddrSet
  Control control_1 (.in_1(DIn));

  assign Dout = {32{1'b0}};
  assign Write = 2'b00;
endmodule

module Control (
  input  [31:0] in_1
);


  // Other names for the same wires on the sheet: OpCode[6:0] = in_1[6:0]; imm4_0[4:0] = in_1[11:7];
  //   rd[4:0] = in_1[11:7]; funct3[2:0] = in_1[14:12]; imm31_12[19:0] = in_1[31:12]; rs1[4:0] = in_1[19:15];
  //   rs2[4:0] = in_1[24:20]; imm11_0[10:0] = in_1[31:21]; funct7[6:0] = in_1[31:25]
endmodule

module PC (
  input  AddrOff,
  input  [31:0] A_IN,
  input  AddrSet,
  input  Clock,
  input  Reset,
  output [31:0] A_Out
);

  wire [31:0] adder_1_out, multiplexer_1_out, multiplexer_2_out;

  Multiplexer #(.enable("false"), .width(32)) multiplexer_1 (
    .in0(32'h4), .in1(A_IN), .out(multiplexer_1_out), .sel(AddrOff));
  Multiplexer #(.enable("false"), .width(32)) multiplexer_2 (
    .in0(adder_1_out), .in1(A_IN), .out(multiplexer_2_out), .sel(AddrSet));
  Adder #(.width(32)) adder_1 (.a(A_Out), .b(multiplexer_1_out), .out(adder_1_out));  // open: cin, cout
  Register #(.width(32)) register_1 (.D(multiplexer_2_out), .Q(A_Out), .clk(Clock), .clr(Reset));  // open: en
endmodule

module MemoryController (
  input  [31:0] Dcur,
  input  [31:0] Din,
  input  [31:0] Ain,
  input  [1:0] Write,
  output [31:0] Dout,
  output [31:0] Aout,
  output write_2
);

  wire and_1_out, and_2_out, and_3_out, and_4_out, and_5_out, and_6_out, decoder_1_out0, decoder_1_out1,
       decoder_1_out2, decoder_1_out3, decoder_2_out0, decoder_2_out2, decoder_2_out3, not_1_out, or_2_out,
       or_3_out, or_4_out, or_5_out;
  wire [31:0] shifter_1_out;

  Shifter #(.width(32)) shifter_1 (.in(Din), .\dist ({Ain[1:0], 3'b000}), .out(shifter_1_out));
  Decoder #(.enable("false"), .select(2)) decoder_1 (
    .out0(decoder_1_out0), .out1(decoder_1_out1), .out2(decoder_1_out2), .out3(decoder_1_out3), .sel(Ain[1:0]));
  Decoder #(.enable("false"), .select(2)) decoder_2 (
    .out0(decoder_2_out0), .out2(decoder_2_out2), .out3(decoder_2_out3), .sel(Write));  // open: out1
  and and_1 (and_1_out, decoder_2_out2, and_3_out);
  not not_1 (not_1_out, decoder_2_out0);
  or or_1 (write_2, Write[0], Write[1]);
  Multiplexer #(.enable("false"), .width(8)) multiplexer_1 (
    .in0(Dcur[7:0]), .in1(shifter_1_out[7:0]), .out(Dout[7:0]), .sel(or_2_out));
  or or_2 (or_2_out, and_3_out, decoder_2_out3);
  or or_3 (or_3_out, and_4_out, and_1_out, decoder_2_out3);
  and and_2 (and_2_out, decoder_2_out2, and_5_out);
  and and_3 (and_3_out, not_1_out, decoder_1_out0);
  and and_4 (and_4_out, not_1_out, decoder_1_out1);
  and and_5 (and_5_out, not_1_out, decoder_1_out2);
  Multiplexer #(.enable("false"), .width(8)) multiplexer_2 (
    .in0(Dcur[15:8]), .in1(shifter_1_out[15:8]), .out(Dout[15:8]), .sel(or_3_out));
  Multiplexer #(.enable("false"), .width(8)) multiplexer_3 (
    .in0(Dcur[23:16]), .in1(shifter_1_out[23:16]), .out(Dout[23:16]), .sel(or_4_out));
  Multiplexer #(.enable("false"), .width(8)) multiplexer_4 (
    .in0(Dcur[31:24]), .in1(shifter_1_out[31:24]), .out(Dout[31:24]), .sel(or_5_out));
  or or_4 (or_4_out, and_5_out, decoder_2_out3);
  or or_5 (or_5_out, and_6_out, and_2_out, decoder_2_out3);
  and and_6 (and_6_out, not_1_out, decoder_1_out3);

  assign Aout = Ain;
endmodule

module TTY (
  input  [31:0] Ain,
  input  [7:0] TTYDin,
  input  \assert ,
  input  [31:0] Din,
  output [31:0] Dout,
  output Dassert,
  output TTYin,
  output TTYout,
  output [7:0] TTYDout
);

  wire [31:8] pull_resistor_1_node;

  Comparator #(.width(32)) comparator_1 (.a(Ain), .b(32'h10000000), .eq(Dassert));  // open: gt, lt
  Pull_Resistor pull_resistor_1 (.node({pull_resistor_1_node, TTYDin}));
  assign Dout = Dassert ? {pull_resistor_1_node, TTYDin} : 32'bz;  // Controlled_Buffer controlled_buffer_1

  assign TTYDout = Din[7:0];
  assign TTYin = Dassert;
  assign TTYout = \assert ;
endmodule

module MemoryDataController (
  input  [31:0] Din,
  input  Enable,
  input  [1:0] LowAddr,
  output [31:0] Din_2
);

  wire [31:0] shifter_1_out;

  Shifter #(.shift("lr"), .width(32)) shifter_1 (.in(Din), .\dist ({LowAddr, 3'b000}), .out(shifter_1_out));
  assign Din_2 = Enable ? shifter_1_out : 32'bz;  // Controlled_Buffer controlled_buffer_1
endmodule
